# Fritzing sketch gatordemo (saved by Fritzing 0.9.3b)

parts:
  CLIP1 = Alligator Clip
  Part1 = Adafruit Circuit Playground Dev Edition [part_number="Adafruit #3000"]  # not connected
  CLIP2 = Alligator Clip
  CLIP3 = Alligator Clip
  Part2 = Flora Bluetooth LE  # not connected
  CLIP4 = Alligator Clip
  CLIP5 = Alligator Clip
  CLIP6 = Alligator Clip
  CLIP7 = Alligator Clip
  CLIP8 = Alligator Clip

nets:
  N1: CLIP1.wire, CLIP6.wire
  N2: CLIP2.wire, CLIP5.wire
  N3: CLIP3.wire, CLIP7.wire
  N4: CLIP4.wire, CLIP8.wire

custom parts:
  Alligator Clip: Alligator clip
  Adafruit Circuit Playground Dev Edition: Would you like to learn electronics, with an all-in-one board that has sensors and LEDs built in? Circuit Playground is here - and it's the best way to practice programming on real hardware with no soldering or sewing required! Circuit Playground features an ATmega32u4 processor, just like our popular Flora. The board's also round and has alligator-clip pads around it so you don't have to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
  Alligator Clip: Alligator clip
  Alligator Clip: Alligator clip
  Flora Bluetooth LE: The Flora Bluefruit LE makes it easy to add Bluetooth Low Energy connectivity to your Flora. Using our Bluefruit iOS App or Android App, you can quickly get your interactive project prototyped by using your iOS or Android phone/tablet as a controller.
  Alligator Clip: Alligator clip
